# Fritzing sketch DeviceSchematics (saved by Fritzing 0.9.3b)
breadboards: 1

parts:
  3_3V = Mini-360 DC-DC Buck converter [package=THT]
  WeMos_D1_Mini1 = WeMos D1 Mini
  V1 = DC Power [voltage=12V]
  Part1 = 12-Channel 16-bit PWM LED Driver
  Bridge1 = LEDs [package=led10mm]
  Bridge2 = LEDs [package=led10mm]
  Stall = LEDs [package=led10mm]
  Phone = LEDs [package=led10mm]
  Lantern2 = LEDs [package=led10mm]
  Lantern1 = LEDs [package=led10mm]
  Lantern3 = LEDs [package=led10mm]
  Part2 = 12-Channel 16-bit PWM LED Driver
  Shop = LEDs [package=led10mm]
  Restaurant = LEDs [package=led10mm]
  Gallery10 = LEDs [package=led10mm]
  Decoration2 = LEDs [package=led10mm]
  Gallery9 = LEDs [package=led10mm]
  Billboard2 = LEDs [package=led10mm]
  Billboard1 = LEDs [package=led10mm]
  BedRoom = LEDs [package=led10mm]
  Gallery6 = LEDs [package=led10mm]
  Gallery5 = LEDs [package=led10mm]
  Gallery4 = LEDs [package=led10mm]
  Part3 = 12-Channel 16-bit PWM LED Driver
  Gallery8 = LEDs [package=led10mm]
  Decoration1 = LEDs [package=led10mm]
  Gallery7 = LEDs [package=led10mm]
  TeaRoom = LEDs [package=led10mm]
  Gallery3 = LEDs [package=led10mm]
  Gallery2 = LEDs [package=led10mm]
  Gallery1 = LEDs [package=led10mm]
  Part4 = 12-Channel 16-bit PWM LED Driver
  Store4 = LEDs [package=led10mm]
  Store3 = LEDs [package=led10mm]
  Store1 = LEDs [package=led10mm]
  Store2 = LEDs [package=led10mm]
  Bar6 = LEDs [package=led10mm]
  Bar5 = LEDs [package=led10mm]
  Bar4 = LEDs [package=led10mm]
  Bar3 = LEDs [package=led10mm]
  Bar2 = LEDs [package=led10mm]
  Bar1 = LEDs [package=led10mm]
  Part5 = 12-Channel 16-bit PWM LED Driver
  Tree2 = LEDs [package=led10mm]
  Tree1 = LEDs [package=led10mm]
  Tower2 = LEDs [package=led10mm]
  Tower1 = LEDs [package=led10mm]
  BathRoom = LEDs [package=led10mm]
  ObstacleLight = LEDs [package=led10mm]

nets:
  GND: 3_3V.IN-, V1.V-, Part1.GND, Part2.GND, Part3.GND, Part4.GND, Part5.GND
  N1: 3_3V.IN+, V1.V+, Part1.V+, Bridge1.A, Bridge2.A, Stall.A, Phone.A, Lantern2.A, Lantern1.A, Lantern3.A, Part2.V+, Shop.A, Restaurant.A, Gallery10.A, Decoration2.A, Gallery9.A, Billboard2.A, Billboard1.A, BedRoom.A, Gallery6.A, Gallery5.A, Gallery4.A, Part3.V+, Gallery8.A, Decoration1.A, Gallery7.A, TeaRoom.A, Gallery3.A, Gallery2.A, Gallery1.A, Part4.V+, Store4.A, Store3.A, Store1.A, Store2.A, Bar6.A, Bar5.A, Bar4.A, Bar3.A, Bar2.A, Bar1.A, Part5.V+, Tree2.A, Tree1.A, Tower2.A, Tower1.A, BathRoom.A, ObstacleLight.A
  N2: 3_3V.OUT+, WeMos_D1_Mini1.3V3
  N3: 3_3V.OUT-, WeMos_D1_Mini1.G
  N4: WeMos_D1_Mini1.D5, Part1.CI
  N5: WeMos_D1_Mini1.D7, Part1.DI
  N6: Part1.DO, Part2.DI
  N7: Part1.CO, Part2.CI
  N8: Part1.R0, Bridge1.C
  N9: Part1.G0, Bridge2.C
  N10: Part1.R1, Stall.C
  N11: Part1.G1, Phone.C
  N12: Part1.B2, Lantern3.C
  N13: Part1.G2, Lantern2.C
  N14: Part1.R2, Lantern1.C
  N15: Part2.DO, Part3.DI
  N16: Part2.CO, Part3.CI
  N17: Part2.R0, Gallery4.C
  N18: Part2.G0, Gallery5.C
  N19: Part2.B0, Gallery6.C
  N20: Part2.R1, BedRoom.C
  N21: Part2.G1, Billboard1.C
  N22: Part2.B1, Billboard2.C
  N23: Part2.G3, Shop.C
  N24: Part2.R3, Restaurant.C
  N25: Part2.B2, Gallery10.C
  N26: Part2.G2, Gallery9.C
  N27: Part2.R2, Decoration2.C
  N28: Part3.DO, Part4.DI
  N29: Part3.CO, Part4.CI
  N30: Part3.R0, Gallery1.C
  N31: Part3.G0, Gallery2.C
  N32: Part3.B0, Gallery3.C
  N33: Part3.R1, TeaRoom.C
  N34: Part3.B2, Gallery8.C
  N35: Part3.G2, Gallery7.C
  N36: Part3.R2, Decoration1.C
  N37: Part4.DO, Part5.DI
  N38: Part4.CO, Part5.CI
  N39: Part4.R0, Bar1.C
  N40: Part4.G0, Bar2.C
  N41: Part4.B0, Bar3.C
  N42: Part4.R1, Bar4.C
  N43: Part4.G1, Bar5.C
  N44: Part4.B1, Bar6.C
  N45: Part4.R3, Store4.C
  N46: Part4.B2, Store3.C
  N47: Part4.G2, Store2.C
  N48: Part4.R2, Store1.C
  N49: Part5.R0, ObstacleLight.C
  N50: Part5.G0, BathRoom.C
  N51: Part5.B0, Tower1.C
  N52: Part5.R1, Tower2.C
  N53: Part5.B3, Tree2.C
  N54: Part5.R3, Tree1.C

custom parts:
  Mini-360 DC-DC Buck converter: Mini-360 DC-DC Buck converter. Tiny buck step down voltage converter, input voltage 4.75 to 23V output 1 to 17V adjustable. Available from ebay and the like.
  WeMos D1 Mini: The D1 mini is a mini wifi board based on ESP-8266EX.
  12-Channel 16-bit PWM LED Driver: The TLC59711 can control 12 separate channels of 16-bit PWM output. Designed (and ideal) for LED control, this board is not good for driving servos. Only three "SPI" pins are required to send data (our Arduino library shows how to use any digital microcontroller pins). Best of all, the design is completely chainable. As long as there's enough power for all the boards you can chain as many as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
